# Fritzing sketch circuit (saved by Fritzing 0.9.3b)
breadboards: 1

parts:
  부품1 = Arduino Uno (Rev3) - ICSP
  M2 = Dagu DGServo 9g (Top view) [part_number=RS001B]
  M3 = Dagu DGServo 9g (Top view) [part_number=RS001B]
  M4 = Dagu DGServo 9g (Top view) [part_number=RS001B]
  S1 = Pushbutton [package="[THT]"]
  S2 = Pushbutton [package="[THT]"]
  S3 = Pushbutton [package="[THT]"]
  부품2 = NRF24L01+ Breakout Board
  R1 = Resistor [tolerance=±5% resistance=10k package="0805 [SMD]"]
  R2 = Resistor [tolerance=±5% resistance=10k package="0805 [SMD]"]
  R3 = Resistor [tolerance=±5% resistance=10k package="0805 [SMD]"]
  VCC1 = Battery block 9V  # not connected

nets:
  N1: 부품1.D9_PWM, 부품2.CS
  N2: 부품1.D10_PWM/SS, 부품2.CE
  N3: 부품1.D11_PWM/MOSI, 부품2.MOSI
  N4: 부품1.D12/MISO, 부품2.MISO
  N5: 부품1.D13/SCK, 부품2.SCK
  GND: 부품1.GND, M2.gnd, M3.gnd, M4.gnd, 부품2.GND, R1.Pin_1, R2.Pin_1, R3.Pin_1
  N6: 부품1.D2, S1.Pin_3, S1.Pin_4, R1.Pin_0
  N7: 부품1.D3_PWM, S2.Pin_3, S2.Pin_4, R2.Pin_0
  N8: 부품1.D4, S3.Pin_3, S3.Pin_4, R3.Pin_0
  N9: 부품1.D5_PWM, M4.pulse
  N10: 부품1.D6_PWM, M3.pulse
  N11: 부품1.D7, M2.pulse
  3V3: 부품1.3V3, 부품2.VCC
  VCC: 부품1.5V, M2.vcc, M3.vcc, M4.vcc, S1.Pin_1, S1.Pin_2, S2.Pin_1, S2.Pin_2, S3.Pin_1, S3.Pin_2
